# Fritzing sketch Sketch (saved by Fritzing 0.9.3b)
perfboards: 1

parts:
  J6 = female pin header, 4 pins [form="♀ (female)"]
  J2 = female pin header, 2 pins [form="♀ (female)"]
  J1 = female pin header, 2 pins [form="♀ (female)"]
  J3 = female pin header, 2 pins [form="♀ (female)"]  # not connected
  J4 = female pin header, 2 pins [form="♀ (female)"]  # not connected
  J5 = female pin header, 4 pins [form="♀ (female)"]
  J8 = female pin header, 3 pins [form="♀ (female)"]
  J9 = female pin header, 4 pins [form="♀ (female)"]
  J7 = female pin header, 4 pins [form="♀ (female)"]

nets:
  N1: J6.pin1, J1.pin2
  N2: J6.pin2, J9.pin4, J7.pin4
  N3: J6.pin3, J9.pin3, J7.pin3
  N4: J6.pin4, J8.pin3
  N5: J2.pin1, J9.pin2, J7.pin2
  N6: J2.pin2, J5.pin2, J5.pin4
  N7: J1.pin1, J9.pin1, J7.pin1
  N8: J5.pin1, J8.pin1
